# Fritzing sketch ESP32_Oled_dht22_css811_bme280 (saved by Fritzing 0.9.3b)
breadboards: 2

parts:
  M1 = DOIT Esp32 DevKit v1 (30 pins long, 11 pins width) [part_number=ESP32S-PIN30]
  Componente1 = SPI OLED Monochrome 128x64 0.96 inch
  Part1 = DHT22 Breakout module [package="Breakout board"]
  Componente2 = Adafruit_BMP280
  Componente3 = Adafruit CCS811 [part_number="Adafruit #3566"]

nets:
  N1: M1.D27, Part1.Out
  N2: M1.D14, Componente1.SCK
  N3: M1.D13, Componente1.SDA
  GND: Componente1.GND, Componente2.GND, Componente3.GND, Componente3.!WAKE
  3.3V: Componente1.VDD, Part1.+, Componente2.3.3V, Componente3.3.3V
  N4: Componente2.SCK/SCL, Componente3.SCL
  N5: Componente2.SDI/SDA, Componente3.SDA

custom parts:
  DOIT Esp32 DevKit v1 (30 pins long, 11 pins width): The DOIT Esp32 DevKit v1 is one of the development board created by DOIT to evaluate the ESP-WROOM-32 module. It is based on the ESP32 microcontroller that boasts Wifi, Bluetooth, Ethernet and Low Power support all in a single chip. (vanepp) made breadboard work, adjusted pin numbering and labels and reduced size of schematic and cleaned up pcb. This chip is 30pins long (2 x15) and 11 pins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
  SPI OLED Monochrome 128x64 0.96 inch: Unknown 128x64 0.96 inch 128x64 SPI Monochrome OLED display
  DHT22 Breakout module: DHT22 temperature and humidity sensor module, provides a low-latency serial interface to measure humidity and temperature.
  Adafruit_BMP280: Bosch has stepped up their game with their new BMP280 sensor, an environmental sensor with temperature, barometric pressure that is the next generation upgrade to the BMP085/BMP180/BMP183. This sensor is great for all sorts of weather sensing and can even be used in both I2C and SPI! This precision sensor from Bosch is the best low-cost, precision sensing solution for measuring barometric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
  Adafruit CCS811: Breathe easy - we finally have an I2C VOC/eCO2 sensor in the Adafruit shop! Add air quality monitoring to your project and with an Adafruit CCS811 Air Quality Sensor Breakout. This sensor from AMS is a gas sensor that can detect a wide range of Volatile Organic Compounds (VOCs) and is intended for indoor air quality monitoring. When connected to your microcontroller (running our library code)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
