# Fritzing sketch iot-8266-starter (saved by Fritzing 0.9.2b)
breadboards: 2

parts:
  U1 = NodeMCU V1.0
  Squix1 = OLED 0.96" 128x64 I2C SSD1306
  R1 = Resistor [tolerance=±5% resistance=10k package="0603 [SMD]"]
  S1 = Momentary Switch [package=ksa_sealed_tac_switch]

nets (from the breadboard view):
  N1: U1.D2, R1.Pin_1, S1.1, S1.2
  3V3: U1.3V3, Squix1.VCC, R1.Pin_0
  GND: U1.GND, Squix1.GND, S1.3, S1.4
  N2: U1.D6, Squix1.SCL
  N3: U1.D7, Squix1.SCA

notes:
  In SSD1306 that I have the VCC and GND are *reversed* from what is shown in this part, please pay attention and read physical labels carefully.

custom parts:
  NodeMCU V1.0: ESP9266 based NodeMCU
